// Logisim project sequencer_logic_gates.circ as structural Verilog: 9 circuits, main circuit display_3_8_3
module display_3_8_3 (
  input  [18:0] x
);

  wire [3:0] bit_bus_conv_1_out_2, bit_bus_conv_2_out_2, bit_bus_conv_3_out_2, bit_bus_conv_4_out_2,
       bit_bus_conv_5_out_2, bit_bus_conv_6_out_2, bit_bus_conv_7_out_2, bit_bus_conv_8_out_2,
       bit_bus_conv_9_out_2, bit_bus_conv_10_out_2, bit_bus_conv_11_out_2, bit_bus_conv_12_out_2,
       bit_bus_conv_13_out_2, bit_bus_conv_14_out_2, bit_bus_conv_15_out_2, bit_bus_conv_16_out_2,
       bit_bus_conv_17_out_2, bit_bus_conv_18_out_2, bit_bus_conv_19_out_2;

  Hex_Digit_Display d18 (.value(bit_bus_conv_1_out_2));  // open: dp
  bit_bus_conv bit_bus_conv_1 (.in_1(x[18]), .out_2(bit_bus_conv_1_out_2));
  Hex_Digit_Display d17 (.value(bit_bus_conv_2_out_2));  // open: dp
  Hex_Digit_Display d16 (.value(bit_bus_conv_3_out_2));  // open: dp
  bit_bus_conv bit_bus_conv_2 (.in_1(x[17]), .out_2(bit_bus_conv_2_out_2));
  bit_bus_conv bit_bus_conv_3 (.in_1(x[16]), .out_2(bit_bus_conv_3_out_2));
  Hex_Digit_Display d15 (.value(bit_bus_conv_4_out_2));  // open: dp
  bit_bus_conv bit_bus_conv_4 (.in_1(x[15]), .out_2(bit_bus_conv_4_out_2));
  Hex_Digit_Display d14 (.value(bit_bus_conv_5_out_2));  // open: dp
  Hex_Digit_Display d13 (.value(bit_bus_conv_6_out_2));  // open: dp
  bit_bus_conv bit_bus_conv_5 (.in_1(x[14]), .out_2(bit_bus_conv_5_out_2));
  bit_bus_conv bit_bus_conv_6 (.in_1(x[13]), .out_2(bit_bus_conv_6_out_2));
  Hex_Digit_Display d12 (.value(bit_bus_conv_7_out_2));  // open: dp
  Hex_Digit_Display d11 (.value(bit_bus_conv_8_out_2));  // open: dp
  bit_bus_conv bit_bus_conv_7 (.in_1(x[12]), .out_2(bit_bus_conv_7_out_2));
  bit_bus_conv bit_bus_conv_8 (.in_1(x[11]), .out_2(bit_bus_conv_8_out_2));
  Hex_Digit_Display d10 (.value(bit_bus_conv_9_out_2));  // open: dp
  bit_bus_conv bit_bus_conv_9 (.in_1(x[10]), .out_2(bit_bus_conv_9_out_2));
  Hex_Digit_Display d9 (.value(bit_bus_conv_10_out_2));  // open: dp
  Hex_Digit_Display d8 (.value(bit_bus_conv_11_out_2));  // open: dp
  bit_bus_conv bit_bus_conv_10 (.in_1(x[9]), .out_2(bit_bus_conv_10_out_2));
  bit_bus_conv bit_bus_conv_11 (.in_1(x[8]), .out_2(bit_bus_conv_11_out_2));
  Hex_Digit_Display d7 (.value(bit_bus_conv_12_out_2));  // open: dp
  bit_bus_conv bit_bus_conv_12 (.in_1(x[7]), .out_2(bit_bus_conv_12_out_2));
  Hex_Digit_Display d6 (.value(bit_bus_conv_13_out_2));  // open: dp
  Hex_Digit_Display d5 (.value(bit_bus_conv_14_out_2));  // open: dp
  bit_bus_conv bit_bus_conv_13 (.in_1(x[6]), .out_2(bit_bus_conv_13_out_2));
  bit_bus_conv bit_bus_conv_14 (.in_1(x[5]), .out_2(bit_bus_conv_14_out_2));
  Hex_Digit_Display d3 (.value(bit_bus_conv_15_out_2));  // open: dp
  Hex_Digit_Display d4 (.value(bit_bus_conv_16_out_2));  // open: dp
  bit_bus_conv bit_bus_conv_15 (.in_1(x[3]), .out_2(bit_bus_conv_15_out_2));
  bit_bus_conv bit_bus_conv_16 (.in_1(x[4]), .out_2(bit_bus_conv_16_out_2));
  Hex_Digit_Display d2 (.value(bit_bus_conv_17_out_2));  // open: dp
  bit_bus_conv bit_bus_conv_17 (.in_1(x[2]), .out_2(bit_bus_conv_17_out_2));
  Hex_Digit_Display d1 (.value(bit_bus_conv_18_out_2));  // open: dp
  Hex_Digit_Display d0 (.value(bit_bus_conv_19_out_2));  // open: dp
  bit_bus_conv bit_bus_conv_18 (.in_1(x[1]), .out_2(bit_bus_conv_18_out_2));
  bit_bus_conv bit_bus_conv_19 (.in_1(x[0]), .out_2(bit_bus_conv_19_out_2));
endmodule

module bit_bus_conv (
  input  in_1,
  output [3:0] out_2
);


  assign out_2 = {3'b000, in_1};
endmodule

module display_16_bit (
  input  [15:0] x
);

  wire [3:0] bit_bus_conv_1_out_2, bit_bus_conv_2_out_2, bit_bus_conv_3_out_2, bit_bus_conv_4_out_2,
       bit_bus_conv_5_out_2, bit_bus_conv_6_out_2, bit_bus_conv_7_out_2, bit_bus_conv_8_out_2,
       bit_bus_conv_9_out_2, bit_bus_conv_10_out_2, bit_bus_conv_11_out_2, bit_bus_conv_12_out_2,
       bit_bus_conv_13_out_2, bit_bus_conv_14_out_2, bit_bus_conv_15_out_2, bit_bus_conv_16_out_2;

  Hex_Digit_Display d15 (.value(bit_bus_conv_1_out_2));  // open: dp
  bit_bus_conv bit_bus_conv_1 (.in_1(x[15]), .out_2(bit_bus_conv_1_out_2));
  Hex_Digit_Display d14 (.value(bit_bus_conv_2_out_2));  // open: dp
  Hex_Digit_Display d13 (.value(bit_bus_conv_3_out_2));  // open: dp
  bit_bus_conv bit_bus_conv_2 (.in_1(x[14]), .out_2(bit_bus_conv_2_out_2));
  bit_bus_conv bit_bus_conv_3 (.in_1(x[13]), .out_2(bit_bus_conv_3_out_2));
  Hex_Digit_Display d12 (.value(bit_bus_conv_4_out_2));  // open: dp
  Hex_Digit_Display d11 (.value(bit_bus_conv_5_out_2));  // open: dp
  bit_bus_conv bit_bus_conv_4 (.in_1(x[12]), .out_2(bit_bus_conv_4_out_2));
  bit_bus_conv bit_bus_conv_5 (.in_1(x[11]), .out_2(bit_bus_conv_5_out_2));
  Hex_Digit_Display d10 (.value(bit_bus_conv_6_out_2));  // open: dp
  bit_bus_conv bit_bus_conv_6 (.in_1(x[10]), .out_2(bit_bus_conv_6_out_2));
  Hex_Digit_Display d9 (.value(bit_bus_conv_7_out_2));  // open: dp
  Hex_Digit_Display d8 (.value(bit_bus_conv_8_out_2));  // open: dp
  bit_bus_conv bit_bus_conv_7 (.in_1(x[9]), .out_2(bit_bus_conv_7_out_2));
  bit_bus_conv bit_bus_conv_8 (.in_1(x[8]), .out_2(bit_bus_conv_8_out_2));
  Hex_Digit_Display d7 (.value(bit_bus_conv_9_out_2));  // open: dp
  bit_bus_conv bit_bus_conv_9 (.in_1(x[7]), .out_2(bit_bus_conv_9_out_2));
  Hex_Digit_Display d6 (.value(bit_bus_conv_10_out_2));  // open: dp
  Hex_Digit_Display d5 (.value(bit_bus_conv_11_out_2));  // open: dp
  bit_bus_conv bit_bus_conv_10 (.in_1(x[6]), .out_2(bit_bus_conv_10_out_2));
  bit_bus_conv bit_bus_conv_11 (.in_1(x[5]), .out_2(bit_bus_conv_11_out_2));
  Hex_Digit_Display d4 (.value(bit_bus_conv_12_out_2));  // open: dp
  Hex_Digit_Display d3 (.value(bit_bus_conv_13_out_2));  // open: dp
  bit_bus_conv bit_bus_conv_12 (.in_1(x[4]), .out_2(bit_bus_conv_12_out_2));
  bit_bus_conv bit_bus_conv_13 (.in_1(x[3]), .out_2(bit_bus_conv_13_out_2));
  Hex_Digit_Display d2 (.value(bit_bus_conv_14_out_2));  // open: dp
  bit_bus_conv bit_bus_conv_14 (.in_1(x[2]), .out_2(bit_bus_conv_14_out_2));
  Hex_Digit_Display d0 (.value(bit_bus_conv_15_out_2));  // open: dp
  Hex_Digit_Display d1 (.value(bit_bus_conv_16_out_2));  // open: dp
  bit_bus_conv bit_bus_conv_15 (.in_1(x[0]), .out_2(bit_bus_conv_15_out_2));
  bit_bus_conv bit_bus_conv_16 (.in_1(x[1]), .out_2(bit_bus_conv_16_out_2));
endmodule

module main (
  input  [7:0] x,
  output [15:0] out_2
);

  wire c, data_path_1_p1, data_path_1_p2;

  Clock clock_1 (.out(c));
  // data_path data_path_1: pin names not known; wires that end beside it: data_path_1_p1, data_path_1_p2, data_path_1_p1, data_path_1_p2, out_2

  // Notes on the sheet:
  //   EDC1 - Lab 6 Microprogramming
  //   Design a sequencer implementing the function given in the task
  //   The data path might require some modifications e.g. adding a sign inverter or a divider.
endmodule

module data_path (
  input  [7:0] x,
  input  c_in_forced,
  input  u_leA,
  input  u_sleA,
  input  u_leB,
  input  u_sreB,
  input  u_clrR,
  input  u_leR,
  input  inv,
  input  x_C,
  output v_z,
  output v_0,
  output [15:0] y_R,
  output [15:0] out_14
);

  wire button_2_out, d_ff_1_q, or_1_out, registerA_p6, registerA_p7, registerA_p8, registerA_p9,
       registerA_p10, registerA_p11, registerA_p12, registerA_p13, registerA_p14, registerA_p15,
       registerA_p16, registerA_p17, registerA_p18, registerA_p19, registerA_p20, registerB_p1, registerB_p6,
       registerB_p7, registerB_p8, registerB_p9, undriven, undriven_2, undriven_3, undriven_4;
  wire [15:0] adder_1_out, and_1_out;
  wire [15:15] not_1_out;

  // Shift_Register registerB: pin names not known; wires that end beside it: registerB_p1, u_leB, u_sreB, x_C, 1'b0, registerB_p6, registerB_p7, registerB_p8, registerB_p9
  Button button_1 (.out(registerB_p1));
  Button button_2 (.out(button_2_out));
  // Shift_Register #(.length(16)) registerA: pin names not known; wires that end beside it: button_2_out, u_leA, u_sleA, x_C, 1'b0, registerA_p6, registerA_p7, registerA_p8, registerA_p9, registerA_p10, registerA_p11, registerA_p12, registerA_p13, registerA_p14, registerA_p15, registerA_p16, registerA_p17, registerA_p18, registerA_p19, registerA_p20, v_0
  xor xor_1 (out_14[0], inv, registerA_p6);
  xor xor_2 (out_14[15], undriven_4, inv);
  nor nor_1 (v_z, registerB_p6, registerB_p7, registerB_p8, registerB_p9, registerA_p18, registerA_p19, registerA_p20, v_0);
  xor xor_3 (out_14[1], inv, registerA_p7);
  xor xor_4 (out_14[2], inv, registerA_p8);
  xor xor_5 (out_14[14], undriven_3, inv);
  xor xor_6 (out_14[3], inv, registerA_p9);
  xor xor_7 (out_14[13], undriven_2, inv);
  xor xor_8 (out_14[4], inv, registerA_p10);
  xor xor_9 (out_14[5], inv, registerA_p11);
  xor xor_10 (out_14[11], registerA_p17, inv);
  xor xor_11 (out_14[12], undriven, inv);
  xor xor_12 (out_14[6], inv, registerA_p12);
  xor xor_13 (out_14[10], registerA_p16, inv);
  xor xor_14 (out_14[7], inv, registerA_p13);
  xor xor_15 (out_14[9], registerA_p15, inv);
  D_Flip_Flop d_ff_1 (.D(c_in_forced), .clk(x_C), .Q(d_ff_1_q));  // open: Qn, preset, reset
  xor xor_16 (out_14[8], inv, registerA_p14);
  not not_1 (not_1_out[15], d_ff_1_q);
  or or_1 (or_1_out, inv, d_ff_1_q);
  assign and_1_out = {16{not_1_out[15]}} & out_14;  // AND_Gate and_1, 16 bits wide
  Adder #(.width(16)) adder_1 (.a(y_R), .b(and_1_out), .out(adder_1_out), .cin(or_1_out));  // open: cout
  Register #(.width(16)) registerR (.D(adder_1_out), .en(u_leR), .clk(x_C), .Q(y_R), .clr(u_clrR));

  // Other names for the same wires on the sheet: c = x_C; c_in = inv; invert = inv

  // Notes on the sheet:
  //   EDC1 - Lab 6 Data path unit
  //   This unit might require introducing small modifications depending on the given task.
endmodule

module grayCodeCounter (
  input  clock,
  output a,
  output b,
  output c,
  output d,
  output e,
  output f
);

  Counter #(.max('h3f), .width(6)) counter_1 (
    .clk(clock), .Q({f, e, d, c, b, a}));  // open: clr, load, up, count, D, carry
endmodule

module SEQUENCER (
  input  ST,
  input  NR,
  input  [7:0] X,
  output [7:0] out_4,
  output [15:0] out_5
);

  wire and_1_out, and_2_out, and_3_out, and_4_out, and_5_out, and_6_out, and_7_out, and_8_out, and_9_out,
       and_10_out, and_11_out, and_12_out, and_13_out, and_14_out, and_15_out, and_16_out, and_19_out,
       and_20_out, and_21_out, and_22_out, and_23_out, and_24_out, button_1_out, c, c_in_forced, inv,
       or_1_out, or_2_out, or_4_out, or_5_out, or_6_out, or_7_out, or_9_out, or_10_out, or_13_out, or_16_out,
       RDY_out, RDY_out_1, RDY_out_2, RDY_out_3, RDY_out_4, RR_out, s0_q, s4_q, s5_q, s6_q, s7_q, s8_q,
       s11_q, s12_q, s14_q, s15_q, s17_q, s18_q, u_leA, u_leA_1, u_leA_2, u_leA_3, u_leB, u_leR, u_leR_1,
       u_leR_3, u_leR_4, u_sleA, undriven, undriven_2, v_0, v_z, xor_1_out;

  D_Flip_Flop s1 (.D(and_12_out), .clk(c), .Q(c_in_forced));  // open: Qn, preset, reset
  D_Flip_Flop s9 (.D(and_16_out), .clk(c), .Q(u_leA_2));  // open: Qn, preset, reset
  D_Flip_Flop s13 (.D(and_22_out), .clk(c), .Q(u_leA_3));  // open: Qn, preset, reset
  D_Flip_Flop s16 (.D(and_20_out), .clk(c), .Q(u_leB));  // open: Qn, preset, reset
  and and_1 (and_1_out, or_10_out, ~v_z);  // AND_Gate
  D_Flip_Flop s2 (.D(c_in_forced), .clk(c), .Q(u_leR_1));  // open: Qn, preset, reset
  D_Flip_Flop s7 (.D(or_1_out), .clk(c), .Q(s7_q));  // open: Qn, preset, reset
  or or_1 (or_1_out, s6_q, and_6_out);
  and and_2 (and_2_out, or_10_out, v_z);
  D_Flip_Flop s18 (.D(and_1_out), .clk(c), .Q(s18_q));  // open: Qn, preset, reset
  D_Flip_Flop s10 (.D(u_leA_2), .clk(c), .Q(u_leR_3));  // open: Qn, preset, reset
  D_Flip_Flop s3 (.D(u_leR_1), .clk(c), .Q(u_leA_1));  // open: Qn, preset, reset
  and and_3 (and_3_out, s7_q, ~NR);  // AND_Gate
  D_Flip_Flop s14 (.D(or_2_out), .clk(c), .Q(s14_q));  // open: Qn, preset, reset
  or or_2 (or_2_out, u_leA_3, and_10_out);
  D_Flip_Flop s17 (.D(RDY_out_4), .clk(c), .Q(s17_q));  // open: Qn, preset, reset
  or or_3 (RDY_out_4, u_leB, and_11_out);
  and and_4 (and_4_out, s18_q, ~v_0);  // AND_Gate
  and and_5 (and_5_out, s18_q, v_0);
  LED RR (.in(RR_out));
  LED RDY (.in(RDY_out));
  D_Flip_Flop s4 (.D(u_leA_1), .clk(c), .Q(s4_q));  // open: Qn, preset, reset
  and and_6 (and_6_out, s7_q, NR);
  D_Flip_Flop s0 (.D(or_4_out), .clk(c), .Q(s0_q));  // open: Qn, preset, reset
  or or_4 (or_4_out, and_24_out, and_9_out);
  D_Flip_Flop s5 (.D(s4_q), .clk(c), .Q(s5_q));  // open: Qn, preset, reset
  or or_5 (or_5_out, u_leR_3, and_14_out);
  and and_7 (and_7_out, s14_q, ~NR);  // AND_Gate
  and and_8 (and_8_out, s17_q, ~NR);  // AND_Gate
  D_Flip_Flop s19 (.D(and_5_out), .clk(c), .Q(u_leR_4));  // open: Qn, preset, reset
  Clock clock_1 (.out(c));
  and and_9 (and_9_out, s0_q, ~NR);  // AND_Gate
  D_Flip_Flop s6 (.D(s5_q), .clk(c), .Q(s6_q));  // open: Qn, preset, reset
  D_Flip_Flop s11 (.D(or_5_out), .clk(c), .Q(s11_q));  // open: Qn, preset, reset
  and and_10 (and_10_out, s14_q, NR);
  and and_11 (and_11_out, s17_q, NR);
  and and_12 (and_12_out, s0_q, NR);
  or or_6 (or_6_out, and_3_out, and_15_out);
  or or_7 (or_7_out, u_leR_4, and_4_out);
  D_Flip_Flop s8 (.D(or_6_out), .clk(c), .Q(s8_q));  // open: Qn, preset, reset
  and and_13 (and_13_out, s11_q, ~NR);  // AND_Gate
  and and_14 (and_14_out, s11_q, NR);
  D_Flip_Flop s20 (.D(or_7_out), .clk(c), .Q(u_sleA));  // open: Qn, preset, reset
  or or_8 (RDY_out_1, or_1_out, or_6_out);
  and and_15 (and_15_out, s8_q, ~NR);  // AND_Gate
  or or_9 (or_9_out, and_7_out, and_19_out);
  or or_10 (or_10_out, and_8_out, u_sleA);
  and and_16 (and_16_out, s8_q, NR);
  or or_11 (RDY_out_3, or_2_out, or_9_out);
  D_Flip_Flop s15 (.D(or_9_out), .clk(c), .Q(s15_q));  // open: Qn, preset, reset
  // AND_Gate and_17 has open pins: in0=undriven, in1=undriven_2, out=open
  // AND_Gate and_18 has open pins: in0=undriven, in1=undriven_2, out=open
  and and_19 (and_19_out, s15_q, ~NR);  // AND_Gate
  and and_20 (and_20_out, s15_q, NR);
  or or_12 (inv, s4_q, s5_q, s6_q);
  D_Flip_Flop s12 (.D(or_13_out), .clk(c), .Q(s12_q));  // open: Qn, preset, reset
  or or_13 (or_13_out, and_13_out, and_21_out);
  or or_14 (RDY_out_2, or_5_out, or_13_out);
  and and_21 (and_21_out, s12_q, ~NR);  // AND_Gate
  and and_22 (and_22_out, s12_q, NR);
  or or_15 (u_leA, u_leA_1, u_leA_2, u_leA_3);
  D_Flip_Flop START (.D(or_16_out), .clk(c), .Q(RR_out));  // open: Qn, preset, reset
  or or_16 (or_16_out, and_2_out, and_23_out);
  or or_17 (u_leR, u_leR_1, inv, u_leR_3, u_leR_4);
  Button button_1 (.out(button_1_out));
  xor xor_1 (xor_1_out, button_1_out, RR_out);
  and and_23 (and_23_out, xor_1_out, ~ST);  // AND_Gate
  and and_24 (and_24_out, xor_1_out, ST);
  or or_18 (RDY_out, RDY_out_1, RDY_out_2, RDY_out_3, RDY_out_4);
  data_path data_path_1 (
    .c_in_forced(c_in_forced), .u_leA(u_leA), .u_sleA(u_sleA), .u_leB(u_leB), .u_sreB(u_sleA),
    .u_clrR(c_in_forced), .u_leR(u_leR), .inv(inv), .x_C(c), .x(X), .y_R(out_5), .v_0(v_0), .v_z(v_z));  // open: out_14

  assign out_4 = X;

  // Other names for the same wires on the sheet: NR_in = NR; ST_in = ST; u_clrR = c_in_forced; u_leR_2 = inv;
  //   u_sreB = u_sleA

  // Notes on the sheet:
  //   //z input
  //   //t input
  //   // +y
  //   //add part z*t
  //   // shift A and B
  //   // +1
  //   // -3x
  //   // f(x) = 1 - 3x + y + z*t
endmodule

module ROM_sequencer (
  input  NR,
  input  ST,
  input  [7:0] X,
  output [7:0] out_4,
  output [15:0] out_5
);

  wire button_1_out, c, multiplexer_1_out, not_1_out, not_2_out, not_3_out, v_0, v_z;
  wire [4:0] counter_1_q;
  wire [18:0] x_t;

  Clock clock_1 (.out(c));
  not not_1 (not_1_out, v_0);
  not not_2 (not_2_out, ST);
  not not_3 (not_3_out, NR);
  ROM #(.addrWidth(5), .dataWidth(19)) rom_1 (.addr(counter_1_q), .data(x_t));
  Multiplexer #(.select(3)) multiplexer_1 (
    .in0(1'b1), .in1(1'b0), .in2(v_z), .in3(not_1_out), .in4(ST), .in5(not_2_out), .in6(NR), .in7(not_3_out),
    .out(multiplexer_1_out), .sel(x_t[18:16]));
  Counter #(.max('h1f), .width(5)) counter_1 (
    .clr(button_1_out), .load(multiplexer_1_out), .clk(c), .D(x_t[4:0]), .Q(counter_1_q));  // open: up, count, carry
  Button button_1 (.out(button_1_out));
  display_3_8_3 display_3_8_3_1 (.x(x_t));
  LED RR (.in(x_t[13]));
  LED RDY (.in(x_t[14]));
  data_path data_path_1 (
    .c_in_forced(x_t[5]), .u_leA(x_t[6]), .u_sleA(x_t[7]), .u_leB(x_t[8]), .u_sreB(x_t[9]), .u_clrR(x_t[10]),
    .u_leR(x_t[11]), .inv(x_t[12]), .x_C(c), .x(X), .y_R(out_5), .v_0(v_0), .v_z(v_z));  // open: out_14

  assign out_4 = X;

  // Other names for the same wires on the sheet: NR_in = NR; ST_in = ST

  // Notes on the sheet:
  //   contents of rom_1 (hex, n*v repeats v):
  //   52000 74001 10423 10894 10045 11806 11807 11808 64008 74009 1004b 1080c 6400c 7400d 1004f 6400f
  //   74010 10112 64012 20017 30016 816 293
  //   // f(x) = 1 - 3x + y + z*t
endmodule

module JK_counter (
  input  clear,
  input  a,
  input  b,
  output Q2,
  output Q1,
  output Q0
);

  wire and_1_out, and_2_out, and_3_out, and_4_out, and_5_out, bcd_to_7_segment_decoder_1_p1,
       bcd_to_7_segment_decoder_1_p2, bcd_to_7_segment_decoder_1_p3, bcd_to_7_segment_decoder_1_p4,
       bcd_to_7_segment_decoder_1_p6, bcd_to_7_segment_decoder_1_p7, bcd_to_7_segment_decoder_1_p8, c,
       or_1_out, or_2_out, xor_1_out, xor_2_out;

  Clock clock_1 (.out(c));
  and and_1 (and_1_out, ~Q0, ~Q1, a);  // AND_Gate
  and and_2 (and_2_out, Q2, a);
  and and_3 (and_3_out, ~a, ~Q2);  // AND_Gate
  xor xor_1 (xor_1_out, a, Q0);
  xor xor_2 (xor_2_out, Q0, a);
  and and_4 (and_4_out, ~a, b, Q1, Q0);  // AND_Gate
  and and_5 (and_5_out, ~Q1, ~Q0);  // AND_Gate
  or or_1 (or_1_out, and_2_out, Q1, and_3_out);
  or or_2 (or_2_out, and_1_out, and_4_out);
  J_K_Flip_Flop jk0 (.J(or_1_out), .K(1'b1), .clk(c), .Q(Q0), .reset(clear));  // open: Qn, preset
  J_K_Flip_Flop jk1 (.J(xor_1_out), .K(xor_2_out), .clk(c), .Q(Q1), .reset(clear));  // open: Qn, preset
  J_K_Flip_Flop jk2 (.J(or_2_out), .K(and_5_out), .clk(c), .Q(Q2), .reset(clear));  // open: Qn, preset
  // BCD_to_7_Segment_decoder bcd_to_7_segment_decoder_1: pin names not known; wires that end beside it: bcd_to_7_segment_decoder_1_p1, bcd_to_7_segment_decoder_1_p2, bcd_to_7_segment_decoder_1_p3, bcd_to_7_segment_decoder_1_p4, {1'b0, Q2, Q1, Q0}, bcd_to_7_segment_decoder_1_p6, bcd_to_7_segment_decoder_1_p7, bcd_to_7_segment_decoder_1_p8
  _7_Segment_Display u_7_segment_display_1 (
    .g(bcd_to_7_segment_decoder_1_p1), .f(bcd_to_7_segment_decoder_1_p3), .a(bcd_to_7_segment_decoder_1_p6),
    .b(bcd_to_7_segment_decoder_1_p8), .e(bcd_to_7_segment_decoder_1_p2), .d(bcd_to_7_segment_decoder_1_p4),
    .c(bcd_to_7_segment_decoder_1_p7));  // open: dp
endmodule
